# Fritzing sketch schmatic (saved by Fritzing 1.0.6)
perfboards: 1

parts:
  HEAD_UP = Sharp PC817 [package=THT]
  IC1 = IC, DIP package, 8 pins [chip_label=8871]  # not connected
  HEAD_DN = Sharp PC817 [package=THT]
  FOOT_UP = Sharp PC817 [package=THT]
  FOOT_DN = Sharp PC817 [package=THT]
  IC2 = IC, DIP package, 8 pins [chip_label=8871]  # not connected
  R1 = Resistor [tolerance=±5% power=0.25W resistance=4.7k package=THT]
  R2 = Resistor [tolerance=±5% power=0.25W resistance=4.7k package=THT]
  R3 = Resistor [tolerance=±5% power=0.25W resistance=4.7k package=THT]
  R4 = Resistor [tolerance=±5% power=0.25W resistance=4.7k package=THT]
  Power = screw terminal, 6 pins
  J2 = double row female pin header, 22 pins [form="♀ (female)"]
  J1 = double row female pin header, 22 pins [form="♀ (female)"]
  J3 = male pin header, 2 pins [form="♂ (male)"]  # not connected
  J4 = shrouded pin header, 10 pins [form="♂ (shrouded male)"]  # not connected
  Buck_In+ = Header 1 [package=pad-1.5x4.5]
  Buck_In- = Header 1 [package=pad-1.5x4.5]
  Buck_Out+ = Header 1 [package=pad-1.5x4.5]
  Buck_Out- = Header 1 [package=pad-1.5x4.5]
  F1 = FUSE [package=fuse_5mm]  # not connected

nets:
  N1: HEAD_UP.Pin_1, R1.Pin_1
  GND: HEAD_UP.Pin_2, HEAD_UP.Pin_3, HEAD_DN.Pin_2, HEAD_DN.Pin_3, FOOT_UP.Pin_2, FOOT_UP.Pin_3, FOOT_DN.Pin_2, FOOT_DN.Pin_3, J1.pin20, Buck_In-.1, Buck_Out-.1
  N2: HEAD_UP.Pin_4, J1.pin5
  N3: HEAD_DN.Pin_1, R2.Pin_1
  N4: HEAD_DN.Pin_4, J1.pin6
  N5: FOOT_UP.Pin_1, R3.Pin_1
  N6: FOOT_UP.Pin_4, J1.pin7
  N7: FOOT_DN.Pin_1, R4.Pin_1
  N8: FOOT_DN.Pin_4, J1.pin8
  HEAD_UP: R1.Pin_0, Power.pin2
  HEAD_DN: R2.Pin_0, Power.pin3
  FOOT_UP: R3.Pin_0, Power.pin4
  N9: R4.Pin_0, Power.pin5
  +29V/29V: Power.pin1, Buck_In+.1
  FOOT_DN: Power.pin6
  5V: J2.pin1, Buck_Out+.1

notes:
  Buck Converter
